// Logisim project lab2_adv.circ as structural Verilog: 14 circuits, main circuit multiplier
module multiplier (
  input  [3:0] a,
  input  [3:0] b,
  output [7:0] p
);

  wire [2:0] and_2_out;
  wire [3:0] and_5_out, and_9_out, and_13_out;
  wire [3:1] adder_1_out, adder_2_out;
  wire [3:3] adder_1_cout, adder_2_cout;

  and and_1 (p[0], a[0], b[0]);
  and and_2 (and_2_out[0], a[1], b[0]);
  and and_3 (and_2_out[1], a[2], b[0]);
  and and_4 (and_2_out[2], a[3], b[0]);
  and and_5 (and_5_out[0], a[0], b[1]);
  and and_6 (and_5_out[1], a[1], b[1]);
  and and_7 (and_5_out[2], a[2], b[1]);
  and and_8 (and_5_out[3], a[3], b[1]);
  and and_9 (and_9_out[0], a[0], b[2]);
  and and_10 (and_9_out[1], a[1], b[2]);
  and and_11 (and_9_out[2], a[2], b[2]);
  and and_12 (and_9_out[3], a[3], b[2]);
  and and_13 (and_13_out[0], a[0], b[3]);
  and and_14 (and_13_out[1], a[1], b[3]);
  and and_15 (and_13_out[2], a[2], b[3]);
  and and_16 (and_13_out[3], a[3], b[3]);
  Adder #(.width(4)) adder_1 (
    .a({1'b0, and_2_out}), .b(and_5_out), .out({adder_1_out, p[1]}), .cout(adder_1_cout[3]));  // open: cin
  Adder #(.width(4)) adder_2 (
    .a({adder_1_cout[3], adder_1_out}), .b(and_9_out), .out({adder_2_out, p[2]}), .cout(adder_2_cout[3]));  // open: cin
  Adder #(.width(4)) adder_3 (
    .a({adder_2_cout[3], adder_2_out}), .b(and_13_out), .out(p[6:3]), .cout(p[7]));  // open: cin
endmodule

module Universal_Gate (
  input  a,
  input  b,
  output c
);

  wire not_1_out;

  and and_1 (c, a, not_1_out);
  not not_1 (not_1_out, b);
endmodule

module ug_not (
  input  in_1,
  output out_2
);

  Universal_Gate Universal_Gate (.a(1'b1), .b(in_1), .c(out_2));
endmodule

module ug_and (
  input  in_1,
  input  in_2,
  output out_3
);

  wire ug_not_out_2;

  Universal_Gate Universal_Gate (.a(in_1), .b(ug_not_out_2), .c(out_3));
  ug_not ug_not (.in_1(in_2), .out_2(ug_not_out_2));
endmodule

module ug_or (
  input  in_1,
  input  in_2,
  output out_3
);

  wire ug_not_out_2, Universal_Gate_c;

  ug_not ug_not (.in_1(in_1), .out_2(ug_not_out_2));
  ug_not ug_not_2 (.in_1(Universal_Gate_c), .out_2(out_3));
  Universal_Gate Universal_Gate (.a(ug_not_out_2), .b(in_2), .c(Universal_Gate_c));
endmodule

module ug_xor (
  input  in_1,
  input  in_2,
  output out_3
);

  wire ug_and_2_out_3, ug_and_out_3, ug_not_out_2;

  ug_and ug_and (.in_1(ug_not_out_2), .in_2(in_2), .out_3(ug_and_out_3));
  ug_not ug_not (.in_1(in_1), .out_2(ug_not_out_2));
  ug_and ug_and_2 (.in_1(in_1), .in_2(in_1), .out_3(ug_and_2_out_3));
  ug_not ug_not_2 (.in_1(in_2), .out_2(in_1));
  ug_or ug_or_1 (.in_1(ug_and_out_3), .in_2(ug_and_2_out_3), .out_3(out_3));
endmodule

module ug_xnor (
  input  in_1,
  input  in_2,
  output out_3
);

  wire ug_and_2_out_3, ug_and_out_3, ug_not_2_out_2, ug_not_out_2;

  ug_not ug_not (.in_1(in_2), .out_2(ug_not_out_2));
  ug_and ug_and (.in_1(in_1), .in_2(in_2), .out_3(ug_and_out_3));
  ug_not ug_not_2 (.in_1(in_1), .out_2(ug_not_2_out_2));
  ug_and ug_and_2 (.in_1(ug_not_2_out_2), .in_2(ug_not_out_2), .out_3(ug_and_2_out_3));
  // ug_or ug_or_1: pin names not known; wires that end beside it: ug_and_out_3, ug_and_2_out_3, out_3
endmodule

module half_adder (
  input  in_1,
  input  in_2,
  output cout,
  output sum
);

  ug_and ug_and (.in_1(in_1), .in_2(in_2), .out_3(cout));
  ug_xor ug_xor (.in_1(in_1), .in_2(in_2), .out_3(sum));
endmodule

module adder (
  input  in_1,
  input  in_2,
  input  cin,
  output cout,
  output sum
);

  wire half_adder_2_cout, half_adder_cout, half_adder_sum;

  half_adder half_adder (.in_1(in_1), .in_2(in_2), .cout(half_adder_cout), .sum(half_adder_sum));
  ug_or ug_or_1 (.in_1(half_adder_cout), .in_2(half_adder_2_cout), .out_3(cout));
  half_adder half_adder_2 (.in_1(half_adder_sum), .in_2(cin), .cout(half_adder_2_cout), .sum(sum));
endmodule

module adder4bit (
  input  [3:0] in_1,
  input  [3:0] in_2,
  output [3:0] out_3,
  output out_4
);

  wire adder_2_cout, adder_3_cout, adder_cout;

  adder adder (.in_1(in_1[0]), .in_2(in_2[0]), .cin(1'b0), .cout(adder_cout), .sum(out_3[0]));
  adder adder_2 (.in_1(in_1[1]), .in_2(in_2[1]), .cin(adder_cout), .cout(adder_2_cout), .sum(out_3[1]));
  adder adder_3 (.in_1(in_1[2]), .in_2(in_2[2]), .cin(adder_2_cout), .cout(adder_3_cout), .sum(out_3[2]));
  adder adder_4 (.in_1(in_1[3]), .in_2(in_2[3]), .cin(adder_3_cout), .cout(out_4), .sum(out_3[3]));
endmodule

module complementer4bit (
  input  [3:0] in_1,
  output [3:0] out_2
);

  wire [3:0] ug_not_out_2;

  ug_not ug_not (.in_1(in_1[0]), .out_2(ug_not_out_2[0]));
  ug_not ug_not_2 (.in_1(in_1[1]), .out_2(ug_not_out_2[1]));
  ug_not ug_not_3 (.in_1(in_1[2]), .out_2(ug_not_out_2[2]));
  ug_not ug_not_4 (.in_1(in_1[3]), .out_2(ug_not_out_2[3]));
  adder4bit adder4bit (.in_1(ug_not_out_2), .in_2(4'b0001), .out_3(out_2));  // open: out_4
endmodule

module suber4bit (
  input  [3:0] a,
  input  [3:0] b,
  output [3:0] dif
);

  wire [3:0] complementer4bit_out_2;

  complementer4bit complementer4bit (.in_1(b), .out_2(complementer4bit_out_2));
  adder4bit adder4bit (.in_1(a), .in_2(complementer4bit_out_2), .out_3(dif));  // open: out_4
endmodule

module ari_r_shift (
  input  [3:0] in_1,
  output [3:0] out_2
);


  assign out_2 = {{2{in_1[3]}}, in_1[2:1]};
endmodule

module cir_l_shift (
  input  [3:0] in_1,
  output [3:0] out_2
);


  assign in_1[2:0] = {3{in_1[3]}};
endmodule
